# Fritzing sketch Ziafati_PoorBehzad_DancingLight (saved by Fritzing 0.9.4)
breadboards: 1

parts:
  Part1 = Arduino Uno (Rev3)
  S1 = Pushbutton [package="[THT]"]
  R1 = Resistor [tolerance=±5% resistance=220 package=THT]
  LED1 = LED - 5mm [color="Red (633nm)" package="5 mm [THT]"]
  LED2 = LED - 5mm [color="Blue (430nm)" package="5 mm [THT]"]
  LED3 = LED - 5mm [color="Yellow (585nm)" package="5 mm [THT]"]
  LED4 = LED - 5mm [color="Green (555nm)" package="5 mm [THT]"]
  R2 = Resistor [tolerance=±5% resistance=220 package=THT]
  R3 = Resistor [tolerance=±5% resistance=220 package=THT]
  R4 = Resistor [tolerance=±5% resistance=220 package=THT]
  R5 = Resistor [tolerance=±5% resistance=220 package=THT]

nets:
  N1: Part1.A0, S1.Pin_1, S1.Pin_2, R1.Pin_0
  N2: Part1.D0/RX, R2.Pin_1
  N3: Part1.D1/TX, R3.Pin_1
  N4: Part1.D2, R4.Pin_1
  N5: Part1.D3_PWM, R5.Pin_1
  N6: Part1.5V, S1.Pin_3, S1.Pin_4, R1.Pin_1, LED1.cathode, LED2.cathode, LED3.cathode, LED4.cathode
  N7: LED1.anode, R4.Pin_0
  N8: LED2.anode, R5.Pin_0
  N9: LED3.anode, R3.Pin_0
  N10: LED4.anode, R2.Pin_0

notes:
  ضیافتی_پوربهزاد
  پروژه: رقص نور(DancingLight)
