# Fritzing sketch Ziafati_PoorBehzad_Green_Yellow_Red (saved by Fritzing 0.9.4)
breadboards: 1

parts:
  Part1 = Arduino Uno (Rev3)
  LED1 = LED - 5mm [color="Green (555nm)" package="5 mm [THT]"]
  LED2 = LED - 5mm [color="Yellow (585nm)" package="5 mm [THT]"]
  LED3 = LED - 5mm [color="Red (633nm)" package="5 mm [THT]"]
  R1 = Resistor [tolerance=±5% resistance=220 package=THT]

nets:
  N1: Part1.D8, LED2.anode
  N2: Part1.D12/MISO, LED3.anode
  N3: Part1.D2, LED1.anode
  N4: Part1.GND, R1.Pin_0
  N5: LED1.cathode, LED2.cathode, LED3.cathode, R1.Pin_1

notes:
  ضیافتی_پوربهزاد
  پروژه: چراغ سبز،زرد،قرمز
