# Fritzing sketch Ziafati_PoorBehzad_PullUp (saved by Fritzing 0.9.4)
breadboards: 1

parts:
  Part1 = Arduino Uno (Rev3)
  S1 = Pushbutton [package="[THT]"]
  R2 = Resistor [tolerance=±5% resistance=220 package=THT]
  LED1 = LED - 5mm [color="Red (633nm)" package="5 mm [THT]"]

nets:
  N1: Part1.D8, S1.Pin_3, S1.Pin_4
  N2: Part1.D2, LED1.anode
  N3: Part1.GND, S1.Pin_1, S1.Pin_2, R2.Pin_0
  N4: R2.Pin_1, LED1.cathode

notes:
  ضیافتی_پوربهزاد
  پروژه PullUp
